# Fritzing sketch sw_project (saved by Fritzing 0.9.3b)
breadboards: 1

parts:
  부품1 = Arduino Mega 2560 (Rev3)
  BT1 = Bluetooth HC-06u [package=THT]
  부품2 = InvenSense MPU6050
  SP1 = SPEAKER [package=pcb_mount_speaker]

nets:
  N1: 부품1.D21/SCL, 부품2.SCL
  N2: 부품1.D20/SDA, 부품2.SDA
  N3: 부품1.D19/RX1, BT1.TXD
  N4: 부품1.D18/TX1, BT1.RXD
  VCC: 부품1.5V, 부품1.D6_PWM, BT1.VCC, 부품2.VCC, SP1.-
  GND: 부품1.GND, BT1.GND, 부품2.GND, SP1.+
  N5: 부품1.D2_PWM, 부품2.INT

custom parts:
  Bluetooth HC-06u: Bluetooth HC-06 - face up, pins down 16.5mm x 37.5mm PCB
